# Fritzing sketch schematic (saved by Fritzing 0.9.0b)
breadboards: 1

parts:
  Part1 = Arduino Mega 2560 (Rev3)
  Raspberry_Pi1 = Raspberry Pi B rev2
  R1 = PHOTOCELL [package=photocell]
  R2 = Resistor [tolerance=±5% resistance=1k package="0603 [SMD]"]
  R3 = PHOTOCELL [package=photocell]
  R4 = Resistor [tolerance=±5% resistance=1k package="0603 [SMD]"]
  R5 = PHOTOCELL [package=photocell]
  R6 = Resistor [tolerance=±5% resistance=1k package="0603 [SMD]"]
  R7 = PHOTOCELL [package=photocell]
  R8 = Resistor [tolerance=±5% resistance=1k package="0603 [SMD]"]
  R9 = PHOTOCELL [package=photocell]
  R10 = PHOTOCELL [package=photocell]
  R11 = PHOTOCELL [package=photocell]
  R12 = PHOTOCELL [package=photocell]
  R13 = Resistor [tolerance=±5% resistance=1k package="0603 [SMD]"]
  R14 = Resistor [tolerance=±5% resistance=1k package="0603 [SMD]"]
  R15 = Resistor [tolerance=±5% resistance=1k package="0603 [SMD]"]
  R16 = Resistor [tolerance=±5% resistance=1k package="0603 [SMD]"]

nets:
  N1: Part1.A0, R1.P$2, R2.Pin_1
  N2: Part1.A1, R3.P$2, R4.Pin_1
  N3: Part1.A2, R5.P$2, R6.Pin_1
  N4: Part1.A3, R7.P$2, R8.Pin_1
  N5: Part1.A4, R12.P$2, R16.Pin_1
  N6: Part1.A5, R11.P$2, R15.Pin_1
  N7: Part1.A6, R10.P$2, R13.Pin_1
  N8: Part1.A7, R9.P$2, R14.Pin_1
  N9: Part1.D21/SCL, Raspberry_Pi1.GPIO_3
  N10: Part1.D20/SDA, Raspberry_Pi1.GPIO_2
  GND: Part1.GND, Raspberry_Pi1.GND, R2.Pin_0, R4.Pin_0, R6.Pin_0, R8.Pin_0, R13.Pin_0, R14.Pin_0, R15.Pin_0, R16.Pin_0
  N11: Part1.5V, R1.P$1, R3.P$1, R5.P$1, R7.P$1, R9.P$1, R10.P$1, R11.P$1, R12.P$1
