# Fritzing sketch schematic_digital (saved by Fritzing 0.9.0b)
breadboards: 1

parts:
  Part1 = Arduino Mega 2560 (Rev3)
  Raspberry_Pi1 = Raspberry Pi B rev2
  S1 = Pushbutton [package="[THT]"]
  S2 = Pushbutton [package="[THT]"]
  S3 = Pushbutton [package="[THT]"]
  S4 = Pushbutton [package="[THT]"]
  S5 = Pushbutton [package="[THT]"]
  S6 = Pushbutton [package="[THT]"]
  S7 = Pushbutton [package="[THT]"]
  S8 = Pushbutton [package="[THT]"]
  R1 = Resistor [tolerance=±5% resistance=1k package="0603 [SMD]"]
  R2 = Resistor [tolerance=±5% resistance=1k package="0603 [SMD]"]
  R3 = Resistor [tolerance=±5% resistance=1k package="0603 [SMD]"]
  R4 = Resistor [tolerance=±5% resistance=1k package="0603 [SMD]"]
  R5 = Resistor [tolerance=±5% resistance=1k package="0603 [SMD]"]
  R6 = Resistor [tolerance=±5% resistance=1k package="0603 [SMD]"]
  R7 = Resistor [tolerance=±5% resistance=1k package="0603 [SMD]"]
  R8 = Resistor [tolerance=±5% resistance=1k package="0603 [SMD]"]

nets:
  N1: Part1.D21/SCL, Raspberry_Pi1.GPIO_3
  N2: Part1.D20/SDA, Raspberry_Pi1.GPIO_2
  GND: Part1.GND, Raspberry_Pi1.GND, R1.Pin_0, R2.Pin_0, R3.Pin_0, R4.Pin_0, R5.Pin_0, R6.Pin_0, R7.Pin_0, R8.Pin_0
  N3: Part1.5V, S1.Pin_3, S1.Pin_4, S2.Pin_3, S2.Pin_4, S3.Pin_3, S3.Pin_4, S4.Pin_3, S4.Pin_4, S5.Pin_3, S5.Pin_4, S6.Pin_3, S6.Pin_4, S7.Pin_3, S7.Pin_4, S8.Pin_3, S8.Pin_4
  N4: Part1.D31, S8.Pin_1, S8.Pin_2, R1.Pin_1
  N5: Part1.D33, S6.Pin_1, S6.Pin_2, R2.Pin_1
  N6: Part1.D35, S7.Pin_1, S7.Pin_2, R3.Pin_1
  N7: Part1.D37, S5.Pin_1, S5.Pin_2, R4.Pin_1
  N8: Part1.D39, S4.Pin_1, S4.Pin_2, R5.Pin_1
  N9: Part1.D41, S3.Pin_1, S3.Pin_2, R7.Pin_1
  N10: Part1.D43, S2.Pin_1, S2.Pin_2, R6.Pin_1
  N11: Part1.D45, S1.Pin_1, S1.Pin_2, R8.Pin_1
